# Fritzing sketch proyecto_comedero (saved by Fritzing 0.9.2b)
circuit board: 9.32739cm x 3.02566cm
breadboards: 1

parts:
  LCM1602_IIC1 = LCM1602 IIC [part_number="LCM1602 IIC" chip_label="LCM1602 IIC" package="DIP (Dual Inline) [THT]"]
  MD09B1 = A4988 Stepper Motor Driver Carrier
  IC1 = DS3231MZ Real Time Clock
  U1 = LCD-16X2 [package=lcd-16x2]
  C1 = Capacitor Polarized [package=cpol-radial-100uf-25v]
  M1 = Stepper Motor - Bipolar
  J1 = Power Jack [package=power_jack_pth_lock]
  M3 = Stepper Motor - Bipolar  # not connected
  Parte1 = Arduino Nano (Rev3.0)
  Part2 = Bluetooth HC-05 Macho
  R1 = Resistor [tolerance=±5% resistance=10k package=THT]
  LM1 = RioRand LM2596

nets (from the breadboard view):
  VSS: LCM1602_IIC1.VSS, U1.VSS
  VDD: LCM1602_IIC1.VDD, U1.VDD
  N1: LCM1602_IIC1.V0, U1.VO
  N2: LCM1602_IIC1.RS, U1.RS
  N3: LCM1602_IIC1.RW, U1.R_W
  N4: LCM1602_IIC1.E, U1.E
  N5: LCM1602_IIC1.D0, U1.DB0
  N6: LCM1602_IIC1.D1, U1.DB1
  N7: LCM1602_IIC1.D2, U1.DB2
  N8: LCM1602_IIC1.D3, U1.DB3
  N9: LCM1602_IIC1.D4, U1.DB4
  N10: LCM1602_IIC1.D5, U1.DB5
  N11: LCM1602_IIC1.D6, U1.DB6
  N12: LCM1602_IIC1.D7, U1.DB7
  N13: LCM1602_IIC1.A, U1.A
  N14: LCM1602_IIC1.K, U1.K
  GND: LCM1602_IIC1.GND, MD09B1.GROUND#147, IC1.Pin_5, Parte1.GND, Part2.GND, LM1.Pin_3
  VCC: LCM1602_IIC1.VCC, MD09B1.VDD, IC1.Pin_2, Parte1.5V, Part2.VCC, R1.Pin_1, LM1.Pin_2
  N15: LCM1602_IIC1.SDA, IC1.Pin_7, Parte1.A4
  N16: LCM1602_IIC1.SCL, IC1.Pin_8, Parte1.A5
  N17: LCM1602_IIC1.LED_A, LCM1602_IIC1.LED_B
  N18: MD09B1.Enable, Parte1.D4, R1.Pin_0
  N19: MD09B1.RESET, MD09B1.SLEEP
  N20: MD09B1.STEP, Parte1.D3
  N21: MD09B1.DIR, Parte1.D2
  N22: MD09B1.VMOT, C1.-, J1.PWR, LM1.Pin_0
  N23: MD09B1.GROUND#141, C1.+, J1.GNDBREAK, LM1.Pin_1
  N24: MD09B1.OUT_2B, M1.A
  N25: MD09B1.OUT_2A, M1.C
  N26: MD09B1.OUT_1A, M1.B
  N27: MD09B1.OUT_1B, M1.D
  N28: Parte1.D5, Part2.TXD
  N29: Parte1.D6, Part2.RXD

custom parts:
  LCM1602 IIC: I2C-Module to use a 1602 or 2004 LCD on with the wire.h libory Serial LCD Modul
  DS3231MZ Real Time Clock: DS3231MZ Real Time Clock. SO-8 surface mount version.
